// Logisim project Lab01_Mux21.circ as structural Verilog: 1 circuit, main circuit main
module main (
  input  sel,
  input  in1,
  input  in2,
  output out1
);

  wire and_1_out, and_2_out, not_1_out, not_2_out;

  not not_1 (not_1_out, sel);
  not not_2 (not_2_out, not_1_out);
  and and_1 (and_1_out, not_2_out, in1);
  and and_2 (and_2_out, not_1_out, in2);
  or or_1 (out1, and_1_out, and_2_out);

  // Notes on the sheet:
  //   Nurbanu Zhenissova
  //   March 28, 2024
  //   Lab 01: 2-Way, 1-Bit Multiplexer
endmodule
