// Logisim project Lab02.circ as structural Verilog: 3 circuits, main circuit main
module Equation_1 (
  input  A1,
  input  B1,
  input  C1,
  output Out1
);

  wire and_1_out, and_2_out, and_3_out;

  and and_1 (and_1_out, ~A1, B1, ~C1);  // AND_Gate
  and and_2 (and_2_out, A1, ~B1, ~C1);  // AND_Gate
  or or_1 (Out1, and_1_out, and_2_out, and_3_out);
  and and_3 (and_3_out, A1, B1, C1);

  // Notes on the sheet:
  //   (A'BC')+(AB'C')+(ABC)
endmodule

module Equation_2 (
  input  A2,
  input  B2,
  input  C2,
  input  D2,
  output Out2
);

  wire and_1_out, and_2_out, and_3_out, and_4_out, not_1_out, not_2_out, not_3_out, not_4_out, not_5_out,
       not_6_out, not_7_out;

  not not_1 (not_1_out, A2);
  not not_2 (not_2_out, B2);
  and and_1 (and_1_out, not_1_out, not_2_out, C2, not_3_out);
  not not_3 (not_3_out, D2);
  not not_4 (not_4_out, A2);
  and and_2 (and_2_out, not_4_out, B2, C2, D2);
  not not_5 (not_5_out, B2);
  and and_3 (and_3_out, A2, not_5_out, C2, not_6_out);
  not not_6 (not_6_out, D2);
  and and_4 (and_4_out, A2, B2, C2, not_7_out);
  not not_7 (not_7_out, D2);
  or or_1 (Out2, and_1_out, and_2_out, and_3_out, and_4_out);

  // Notes on the sheet:
  //   (A'B'CD')+(A'BCD)+(AB'CD')+(ABCD')
  //   (A'BC')+(AB'C')+(ABC)
endmodule

module main (
  input  A1,
  input  B1,
  input  C1,
  input  A2,
  input  B2,
  input  C2,
  input  D2,
  output Out1,
  output Out2
);

  Equation_1 equation_1_1 (.A1(A1), .B1(B1), .C1(C1), .Out1(Out1));
  Equation_2 equation_2_1 (.A2(A2), .B2(B2), .C2(C2), .D2(D2), .Out2(Out2));
endmodule
