// Logisim project Lab03.circ as structural Verilog: 2 circuits, main circuit main
module main (
  input  In1,
  input  In2,
  input  In3,
  input  In4,
  input  In5,
  input  In6,
  input  In7,
  input  In8,
  input  In9,
  output [3:0] PriOut
);

  Hex_Digit_Display hex_digit_display_1 (.value(PriOut));  // open: dp
  Encoder encoder_1 (
    .In1(In1), .In2(In2), .In3(In3), .In4(In4), .In5(In5), .In6(In6), .In7(In7), .In8(In8), .In9(In9),
    .Out1(PriOut[0]), .Out2(PriOut[1]), .Out3(PriOut[2]), .Out4(PriOut[3]));
endmodule

module Encoder (
  input  In1,
  input  In2,
  input  In3,
  input  In4,
  input  In5,
  input  In6,
  input  In7,
  input  In8,
  input  In9,
  output Out1,
  output Out2,
  output Out3,
  output Out4
);

  wire not_1_out, not_2_out, not_3_out, not_4_out, not_5_out, not_6_out, not_7_out, not_8_out, not_9_out,
       not_10_out, U1_out, U2_out, U3_out, U4_out, U5_out, U6_out, U7_out, U8_out, U9_out, U10_out, U11_out,
       U12_out, U16_out;

  not not_1 (not_1_out, In2);
  not not_2 (not_2_out, In4);
  not not_3 (not_3_out, In6);
  not not_4 (not_4_out, In4);
  not not_5 (not_5_out, In6);
  not not_6 (not_6_out, In6);
  not not_7 (not_7_out, In4);
  not not_8 (not_8_out, In5);
  not not_9 (not_9_out, In4);
  not not_10 (not_10_out, In5);
  nor U16 (U16_out, In8, In9);
  and U1 (U1_out, In1, not_1_out, not_2_out, not_3_out, U16_out);
  and U2 (U2_out, In3, not_4_out, not_5_out, U16_out);
  and U3 (U3_out, In5, not_6_out, U16_out);
  or U13 (Out1, U1_out, U2_out, U3_out, U4_out, In9);
  and U4 (U4_out, In7, U16_out);
  and U5 (U5_out, In2, not_7_out, not_8_out, U16_out);
  and U6 (U6_out, not_9_out, not_10_out, In3, U16_out);
  or U14 (Out2, U5_out, U6_out, U7_out, U8_out);
  and U7 (U7_out, In6, U16_out);
  and U8 (U8_out, In7, U16_out);
  and U9 (U9_out, In4, U16_out);
  and U10 (U10_out, In5, U16_out);
  or U15 (Out3, U9_out, U10_out, U11_out, U12_out);
  and U11 (U11_out, In6, U16_out);
  and U12 (U12_out, In7, U16_out);
  or U17 (Out4, In9, In8);
endmodule
